# Fritzing sketch bela-module-proto (saved by Fritzing 0.9.3b)
perfboards: 1

parts:
  Part1 = Bela  # not connected
  IC1 = IC, DIP package, 14 pins [chip_label=CD4504]  # not connected
  IC2 = IC, DIP package, 14 pins [chip_label=CD4504]  # not connected
  IC3 = IC, DIP package, 14 pins [chip_label=CD4504]
  IC4 = IC, DIP package, 14 pins [chip_label=LM324n]
  IC5 = IC, DIP package, 14 pins [chip_label=LM324n]
  IC6 = IC, DIP package, 14 pins [chip_label=LM324n]
  U1 = Voltage Regulator - 5V [package="TO220 [THT]"]
  J2 = male pin header, 5 pins [form="♂ (male)"]  # not connected
  J4 = male pin header, 5 pins [form="♂ (male)"]  # not connected

nets:
  N1: IC3.pin9, IC6.pin10
  N2: IC4.pin4, U1.output_voltage
  N3: IC4.pin13, IC6.pin8
  N4: IC5.pin4, IC6.pin1
  N5: IC5.pin6, IC6.pin2

notes:
  +12 GND GND GND -12

custom parts:
  Bela: Bela low-latency audio/sensor platform
